# Fritzing sketch kartino (saved by Fritzing 0.8.5b)

parts:
  Componente1 = Arduino Micro (Rev3)
  Componente2 = Triple Axis Accelerometer Breakout - ADXL335
  Componente3 = OpenLog  # not connected

nets:
  GND: Componente1.GND, Componente2.GND
  N1: Componente1.A2, Componente2.ZOUT
  N2: Componente1.A1, Componente2.YOUT
  N3: Componente1.A0, Componente2.XOUT
  3V3: Componente1.3V3, Componente2.VCC
