# Fritzing sketch with-OpenLog (saved by Fritzing 0.8.5b)

parts:
  Componente1 = Arduino Micro (Rev3)
  Componente2 = Triple Axis Accelerometer Breakout - ADXL335
  Componente3 = OpenLog
  VCC1 = Battery block 9V

nets:
  N1: Componente1.MOSI, Componente3.MISO
  GND: Componente1.GND, Componente2.GND, Componente3.GND, VCC1.-
  N2: Componente1.SCK, Componente3.SCK
  N3: Componente1.MISO, Componente3.MOSI
  N4: Componente1.VIN, VCC1.+
  5V: Componente1.5V, Componente3.VCC
  N5: Componente1.A2, Componente2.ZOUT
  N6: Componente1.A1, Componente2.YOUT
  N7: Componente1.A0, Componente2.XOUT
  3V3: Componente1.3V3, Componente2.VCC
